# Fritzing sketch abismo_Pulso_GSR (saved by Fritzing 0.9.3b)
breadboards: 1

parts:
  HC_05 = Bluetooth HC-05 Macho
  Pulse_Sensor = Pulse Sensor (not original) [package=THT]
  Microcontrolador = Arduino Uno (Rev3)
  R1 = Resistor [tolerance=±5% resistance=220 package=THT]
  LED1 = LED - 5mm [color="Red (633nm)" package="5 mm [THT]"]
  P1 = GSR [package=THT]
  R2 = Resistor [tolerance=±5% resistance=1k package=THT]
  R3 = Resistor [tolerance=±5% resistance=1k package=THT]
  104 = Capacitor [part_number=104 package=cap-pth-small2]  # not connected
  Part1 = Arduino Pro Mini v13  # not connected

nets (from the schematic view):
  N1: HC_05.TXD, Microcontrolador.D10_PWM/SS
  N2: HC_05.RXD, Microcontrolador.D11_PWM/MOSI
  VCC: HC_05.VCC, Pulse_Sensor.+, Microcontrolador.5V, P1.+
  GND: HC_05.GND, Pulse_Sensor.-, Microcontrolador.GND, LED1.cathode, R2.Pin_1, R3.Pin_1
  N3: Pulse_Sensor.Sig, Microcontrolador.A0
  N4: Microcontrolador.A1, P1.-, R2.Pin_0, R3.Pin_0
  N5: Microcontrolador.D5_PWM, R1.Pin_0
  N6: R1.Pin_1, LED1.anode

custom parts:
  Pulse Sensor (not original): Pulse Sensor
  GSR: GSR Sensor de Resistencia Galvanica
