# Fritzing sketch abismo_Pulso_GSR_proMini (saved by Fritzing 0.9.3b)
circuit board: 6.44755cm x 4.57007cm
breadboards: 1

parts:
  HC_05 = Bluetooth HC-05 Macho
  Pulse_Sensor = Pulse Sensor (not original) [package=THT]
  R1 = Resistor [tolerance=±5% resistance=220 package=THT]
  GSR = GSR [package=THT]
  R2 = Resistor [tolerance=±5% resistance=100k package=THT]
  R3 = Resistor [tolerance=±5% resistance=100k package=THT]
  104 = Capacitor [part_number=104 package=cap-pth-small2]
  Part1 = Arduino Pro Mini v13
  S1 = Toggle Switch [package=THT]
  BAT1 = BC9VPC [package=bc9vpc]
  LED1 = LED - 5mm [color="Red (633nm)" package="5 mm [THT]"]

nets (from the pcb view):
  N1: HC_05.TXD, Part1.D10_PWM/SS
  N2: HC_05.RXD, Part1.D11_PWM/MOSI
  VCC: HC_05.VCC, Pulse_Sensor.+, GSR.+, Part1.VCC, S1.L1
  GND: HC_05.GND, Pulse_Sensor.-, R3.Pin_1, 104.1, Part1.GND, BAT1.V-, LED1.cathode
  N3: Pulse_Sensor.Sig, Part1.A1
  N4: R1.Pin_0, LED1.anode
  N5: R1.Pin_1, Part1.D5_PWM
  N6: R2.Pin_0, R3.Pin_0
  N7: R2.Pin_1, 104.2, Part1.A0
  N8: S1.COM, BAT1.V+

custom parts:
  Pulse Sensor (not original): Pulse Sensor
  GSR: GSR Sensor de Resistencia Galvanica
